// Logisim project OiAK_P.circ as structural Verilog: 10 circuits, main circuit preprocessing
module preprocessing (
  input  a_i,
  input  b_i,
  output g_i_AND,
  output h_i_XOR,
  output p_i_OR
);

  wire not_1_out;

  and and_1 (g_i_AND, a_i, b_i);
  or or_1 (p_i_OR, a_i, b_i);
  not not_1 (not_1_out, g_i_AND);
  and and_2 (h_i_XOR, not_1_out, p_i_OR);

  // Notes on the sheet:
  //   KWADRAT
endmodule

module black_dot (
  input  p_i,
  input  p_i_prev,
  input  g_i,
  input  g_i_prev,
  output g_i_i_prev,
  output p_i_i_prev
);

  wire and_1_out;

  and and_1 (and_1_out, g_i_prev, p_i);
  or or_1 (g_i_i_prev, g_i, and_1_out);
  and and_2 (p_i_i_prev, p_i, p_i_prev);
endmodule

module Delay (
  input  g_i,
  input  p_i,
  output g_i_delay,
  output p_i_delay
);

  buf buffer_1 (g_i_delay, g_i);
  buf buffer_2 (p_i_delay, p_i);
endmodule

module n_striped (
  input  a_i,
  input  b_i,
  output g_i_or_b_i_next_k0,
  output p_i_or_b_i_next_k1,
  output h_i_or_a_i_k0,
  output a_i_k1
);

  wire not_1_out;

  and and_1 (g_i_or_b_i_next_k0, a_i, b_i);
  not not_1 (not_1_out, g_i_or_b_i_next_k0);
  and and_2 (h_i_or_a_i_k0, not_1_out, p_i_or_b_i_next_k1);
  not not_2 (a_i_k1, h_i_or_a_i_k0);
  or or_1 (p_i_or_b_i_next_k1, a_i, b_i);
endmodule

module n_X (
  input  B_i_prev,
  input  A_i,
  output g_i_prim,
  output p_i_prim,
  output h_i_prim
);

  wire not_1_out;

  and and_1 (g_i_prim, A_i, B_i_prev);
  not not_1 (not_1_out, g_i_prim);
  or or_1 (p_i_prim, A_i, B_i_prev);
  and and_2 (h_i_prim, not_1_out, p_i_prim);
endmodule

module Proposed_Modulo (
  input  B6,
  input  A6,
  input  B5,
  input  A5,
  input  B4,
  input  A4,
  input  B3,
  input  A3,
  input  B2,
  input  A2,
  input  B1,
  input  A1,
  input  B0,
  input  A0,
  input  K6,
  input  K5,
  input  K4,
  input  K3,
  input  K2,
  input  K1,
  input  K0,
  output out_22,
  output S6,
  output S5,
  output S4,
  output S3,
  output S2,
  output S1,
  output S0
);

  wire black_dot_1_g_i_i_prev, black_dot_1_p_i_i_prev, black_dot_3_g_i_i_prev, black_dot_3_p_i_i_prev,
       black_dot_4_g_i_i_prev, black_dot_4_p_i_i_prev, black_dot_5_g_i_i_prev, black_dot_5_p_i_i_prev,
       black_dot_6_g_i_i_prev, black_dot_6_p_i_i_prev, black_dot_7_g_i_i_prev, black_dot_7_p_i_i_prev,
       black_dot_8_g_i_i_prev, black_dot_8_p_i_i_prev, C0_g_i_delay, C0_p_g_i_delay, C1_g_i_delay,
       C1_p_g_i_delay, C1_p_i_delay, C1_p_p_i_delay, C2_g_i_delay, C2_p_g_i_delay, C2_p_i_delay,
       C2_p_p_i_delay, C3_g_i_delay, C3_p_g_i_delay, C3_p_i_delay, C3_p_p_i_delay, C4_g_i_i_prev,
       C4_p_g_i_i_prev, C4_p_i_i_prev, C4_p_p_i_i_prev, C5_g_i_i_prev, C5_p_g_i_i_prev, C5_p_i_i_prev,
       C5_p_p_i_i_prev, calc_carry_1_c_i, calc_carry_2_c_i, calc_carry_3_c_i, calc_carry_4_c_i,
       calc_carry_5_c_i, calc_carry_6_c_i, calc_carry_7_c_i, calc_carry_8_c_i, calc_carry_9_c_i,
       calc_carry_10_c_i, calc_carry_11_c_i, controlled_buffer_1_a_i, controlled_buffer_2_a_i,
       controlled_buffer_2_b_i_next, controlled_buffer_3_a_i, controlled_buffer_3_b_i_next,
       controlled_buffer_4_a_i, controlled_buffer_4_b_i_next, controlled_buffer_5_a_i,
       controlled_buffer_5_b_i_next, controlled_buffer_6_a_i, controlled_buffer_6_b_i_next,
       controlled_buffer_7_a_i, controlled_buffer_7_b_i_next, Cout_out, delay_1_g_i_delay, delay_1_p_i_delay,
       delay_2_g_i_delay, delay_2_p_i_delay, delay_3_g_i_delay, delay_3_p_i_delay, delay_4_g_i_delay,
       delay_4_p_i_delay, delay_5_g_i_delay, delay_5_p_i_delay, delay_6_g_i_delay, delay_6_p_i_delay,
       delay_7_g_i_delay, delay_7_p_i_delay, delay_8_g_i_delay, delay_8_p_i_delay, h_delay_1_h_0_d,
       h_delay_1_h_1_d, h_delay_1_h_2_d, h_delay_1_h_3_d, h_delay_1_h_4_d, h_delay_1_h_5_d, h_delay_1_h_6_d,
       h_delay_2_h_0_d, h_delay_2_h_1_d, h_delay_2_h_2_d, h_delay_2_h_3_d, h_delay_2_h_4_d, h_delay_2_h_5_d,
       h_delay_2_h_6_d, h_delay_3_h_0_d, h_delay_3_h_1_d, h_delay_3_h_2_d, h_delay_3_h_3_d, h_delay_3_h_4_d,
       h_delay_3_h_5_d, h_delay_3_h_6_d, h_delay_4_h_0_d, h_delay_4_h_1_d, h_delay_4_h_2_d, h_delay_4_h_3_d,
       h_delay_4_h_4_d, h_delay_4_h_5_d, h_delay_4_h_6_d, h_delay_5_h_0_d, h_delay_5_h_1_d, h_delay_5_h_2_d,
       h_delay_5_h_3_d, h_delay_5_h_4_d, h_delay_5_h_5_d, h_delay_5_h_6_d, n_striped_1_a_i_k1,
       n_striped_1_g_i_or_b_i_next_k0, n_striped_1_h_i_or_a_i_k0, n_striped_1_p_i_or_b_i_next_k1,
       n_striped_2_a_i_k1, n_striped_2_g_i_or_b_i_next_k0, n_striped_2_h_i_or_a_i_k0,
       n_striped_2_p_i_or_b_i_next_k1, n_striped_3_a_i_k1, n_striped_3_g_i_or_b_i_next_k0,
       n_striped_3_h_i_or_a_i_k0, n_striped_3_p_i_or_b_i_next_k1, n_striped_4_a_i_k1,
       n_striped_4_g_i_or_b_i_next_k0, n_striped_4_h_i_or_a_i_k0, n_striped_4_p_i_or_b_i_next_k1,
       n_striped_5_a_i_k1, n_striped_5_g_i_or_b_i_next_k0, n_striped_5_h_i_or_a_i_k0,
       n_striped_5_p_i_or_b_i_next_k1, n_striped_6_a_i_k1, n_striped_6_g_i_or_b_i_next_k0,
       n_striped_6_h_i_or_a_i_k0, n_striped_6_p_i_or_b_i_next_k1, n_striped_7_a_i_k1,
       n_striped_7_g_i_or_b_i_next_k0, n_striped_7_h_i_or_a_i_k0, n_striped_7_p_i_or_b_i_next_k1,
       n_x_1_g_i_prim, n_x_1_h_i_prim, n_x_1_p_i_prim, n_x_2_g_i_prim, n_x_2_h_i_prim, n_x_2_p_i_prim,
       n_x_3_g_i_prim, n_x_3_h_i_prim, n_x_3_p_i_prim, n_x_4_g_i_prim, n_x_4_h_i_prim, n_x_4_p_i_prim,
       n_x_5_g_i_prim, n_x_5_h_i_prim, n_x_5_p_i_prim, n_x_6_g_i_prim, n_x_6_h_i_prim, n_x_6_p_i_prim,
       n_x_7_g_i_prim, n_x_7_h_i_prim, n_x_7_p_i_prim, normal0_g_i_delay, normal0_p_i_delay,
       normal1_g_i_delay, normal1_p_i_delay, normal2_g_i_i_prev, normal2_p_i_i_prev, normal3_g_i_i_prev,
       normal3_p_i_i_prev, normal4_g_i_delay, normal4_p_i_delay, normal5_g_i_delay, normal5_p_i_delay,
       normal6_g_i_i_prev, normal6_p_i_i_prev, prim0_g_i_delay, prim0_p_i_delay, prim1_g_i_delay,
       prim1_p_i_delay, prim2_g_i_i_prev, prim2_p_i_i_prev, prim3_g_i_i_prev, prim3_p_i_i_prev,
       prim4_g_i_delay, prim4_p_i_delay, prim5_g_i_delay, prim5_p_i_delay, prim6_g_i_i_prev,
       prim6_p_i_i_prev, Prim_h_0_d, Prim_h_1_d, Prim_h_2_d, Prim_h_3_d, Prim_h_4_d, Prim_h_5_d, Prim_h_6_d;

  Calc_Carry calc_carry_1 (
    .G_prev(black_dot_1_g_i_i_prev), .P_prev(black_dot_1_p_i_i_prev), .C_prev(calc_carry_3_c_i),
    .C_i(calc_carry_1_c_i));
  H_delay h_delay_1 (
    .H_6(n_striped_1_h_i_or_a_i_k0), .H_5(n_striped_2_h_i_or_a_i_k0), .H_4(n_striped_3_h_i_or_a_i_k0),
    .H_3(n_striped_4_h_i_or_a_i_k0), .H_2(n_striped_5_h_i_or_a_i_k0), .H_1(n_striped_6_h_i_or_a_i_k0),
    .H_0(n_striped_7_h_i_or_a_i_k0), .H_6_d(h_delay_1_h_6_d), .H_5_d(h_delay_1_h_5_d),
    .H_4_d(h_delay_1_h_4_d), .H_3_d(h_delay_1_h_3_d), .H_2_d(h_delay_1_h_2_d), .H_1_d(h_delay_1_h_1_d),
    .H_0_d(h_delay_1_h_0_d));
  H_delay h_delay_2 (
    .H_6(h_delay_1_h_6_d), .H_5(h_delay_1_h_5_d), .H_4(h_delay_1_h_4_d), .H_3(h_delay_1_h_3_d),
    .H_2(h_delay_1_h_2_d), .H_1(h_delay_1_h_1_d), .H_0(h_delay_1_h_0_d), .H_6_d(h_delay_2_h_6_d),
    .H_5_d(h_delay_2_h_5_d), .H_4_d(h_delay_2_h_4_d), .H_3_d(h_delay_2_h_3_d), .H_2_d(h_delay_2_h_2_d),
    .H_1_d(h_delay_2_h_1_d), .H_0_d(h_delay_2_h_0_d));
  H_delay h_delay_3 (
    .H_6(h_delay_2_h_6_d), .H_5(h_delay_2_h_5_d), .H_4(h_delay_2_h_4_d), .H_3(h_delay_2_h_3_d),
    .H_2(h_delay_2_h_2_d), .H_1(h_delay_2_h_1_d), .H_0(h_delay_2_h_0_d), .H_6_d(h_delay_3_h_6_d),
    .H_5_d(h_delay_3_h_5_d), .H_4_d(h_delay_3_h_4_d), .H_3_d(h_delay_3_h_3_d), .H_2_d(h_delay_3_h_2_d),
    .H_1_d(h_delay_3_h_1_d), .H_0_d(h_delay_3_h_0_d));
  H_delay h_delay_4 (
    .H_6(n_x_1_h_i_prim), .H_5(n_x_2_h_i_prim), .H_4(n_x_3_h_i_prim), .H_3(n_x_4_h_i_prim),
    .H_2(n_x_5_h_i_prim), .H_1(n_x_6_h_i_prim), .H_0(n_x_7_h_i_prim), .H_6_d(h_delay_4_h_6_d),
    .H_5_d(h_delay_4_h_5_d), .H_4_d(h_delay_4_h_4_d), .H_3_d(h_delay_4_h_3_d), .H_2_d(h_delay_4_h_2_d),
    .H_1_d(h_delay_4_h_1_d), .H_0_d(h_delay_4_h_0_d));
  H_delay h_delay_5 (
    .H_6(h_delay_4_h_6_d), .H_5(h_delay_4_h_5_d), .H_4(h_delay_4_h_4_d), .H_3(h_delay_4_h_3_d),
    .H_2(h_delay_4_h_2_d), .H_1(h_delay_4_h_1_d), .H_0(h_delay_4_h_0_d), .H_6_d(h_delay_5_h_6_d),
    .H_5_d(h_delay_5_h_5_d), .H_4_d(h_delay_5_h_4_d), .H_3_d(h_delay_5_h_3_d), .H_2_d(h_delay_5_h_2_d),
    .H_1_d(h_delay_5_h_1_d), .H_0_d(h_delay_5_h_0_d));
  H_delay Prim (
    .H_6(h_delay_5_h_6_d), .H_5(h_delay_5_h_5_d), .H_4(h_delay_5_h_4_d), .H_3(h_delay_5_h_3_d),
    .H_2(h_delay_5_h_2_d), .H_1(h_delay_5_h_1_d), .H_0(h_delay_5_h_0_d), .H_6_d(Prim_h_6_d),
    .H_5_d(Prim_h_5_d), .H_4_d(Prim_h_4_d), .H_3_d(Prim_h_3_d), .H_2_d(Prim_h_2_d), .H_1_d(Prim_h_1_d),
    .H_0_d(Prim_h_0_d));
  Calc_Carry calc_carry_2 (
    .G_prev(C5_p_g_i_i_prev), .P_prev(C5_p_p_i_i_prev), .C_prev(calc_carry_4_c_i), .C_i(calc_carry_2_c_i));
  n_striped n_striped_1 (
    .a_i(A6), .b_i(B6), .g_i_or_b_i_next_k0(n_striped_1_g_i_or_b_i_next_k0),
    .p_i_or_b_i_next_k1(n_striped_1_p_i_or_b_i_next_k1), .h_i_or_a_i_k0(n_striped_1_h_i_or_a_i_k0),
    .a_i_k1(n_striped_1_a_i_k1));
  Controlled_Buffer controlled_buffer_1 (
    .B_K0(n_striped_1_g_i_or_b_i_next_k0), .B_K1(n_striped_1_p_i_or_b_i_next_k1),
    .A_K0(n_striped_1_h_i_or_a_i_k0), .A_K1(n_striped_1_a_i_k1), .K_i(K6), .B_i_next(out_22),
    .A_i(controlled_buffer_1_a_i));
  n_X n_x_1 (
    .B_i_prev(controlled_buffer_2_b_i_next), .A_i(controlled_buffer_1_a_i), .g_i_prim(n_x_1_g_i_prim),
    .p_i_prim(n_x_1_p_i_prim), .h_i_prim(n_x_1_h_i_prim));
  Delay delay_1 (
    .g_i(n_x_1_g_i_prim), .p_i(n_x_1_p_i_prim), .g_i_delay(delay_1_g_i_delay), .p_i_delay(delay_1_p_i_delay));
  black_dot prim6 (
    .p_i(delay_1_p_i_delay), .p_i_prev(black_dot_3_p_i_i_prev), .g_i(delay_1_g_i_delay),
    .g_i_prev(black_dot_3_g_i_i_prev), .g_i_i_prev(prim6_g_i_i_prev), .p_i_i_prev(prim6_p_i_i_prev));
  black_dot black_dot_1 (
    .p_i(prim6_p_i_i_prev), .p_i_prev(prim3_p_i_i_prev), .g_i(prim6_g_i_i_prev), .g_i_prev(prim3_g_i_i_prev),
    .g_i_i_prev(black_dot_1_g_i_i_prev), .p_i_i_prev(black_dot_1_p_i_i_prev));
  Calc_Carry calc_carry_3 (
    .G_prev(C5_g_i_i_prev), .P_prev(C5_p_i_i_prev), .C_prev(calc_carry_5_c_i), .C_i(calc_carry_3_c_i));
  Tristate_Based_MUX tristate_based_mux_1 (
    .C_out(calc_carry_1_c_i), .H_i(h_delay_3_h_6_d), .H_i_prim(Prim_h_6_d), .C_i_prev(calc_carry_3_c_i),
    .C_i_prim_prev(calc_carry_2_c_i), .S_i(S6));
  Delay delay_2 (
    .g_i(n_striped_1_g_i_or_b_i_next_k0), .p_i(n_striped_1_p_i_or_b_i_next_k1),
    .g_i_delay(delay_2_g_i_delay), .p_i_delay(delay_2_p_i_delay));
  black_dot normal6 (
    .p_i(delay_2_p_i_delay), .p_i_prev(black_dot_4_p_i_i_prev), .g_i(delay_2_g_i_delay),
    .g_i_prev(black_dot_4_g_i_i_prev), .g_i_i_prev(normal6_g_i_i_prev), .p_i_i_prev(normal6_p_i_i_prev));
  black_dot black_dot_2 (
    .p_i(normal6_p_i_i_prev), .p_i_prev(normal3_p_i_i_prev), .g_i(normal6_g_i_i_prev),
    .g_i_prev(normal3_g_i_i_prev));  // open: g_i_i_prev, p_i_i_prev
  n_striped n_striped_2 (
    .a_i(A5), .b_i(B5), .g_i_or_b_i_next_k0(n_striped_2_g_i_or_b_i_next_k0),
    .p_i_or_b_i_next_k1(n_striped_2_p_i_or_b_i_next_k1), .h_i_or_a_i_k0(n_striped_2_h_i_or_a_i_k0),
    .a_i_k1(n_striped_2_a_i_k1));
  Controlled_Buffer controlled_buffer_2 (
    .B_K0(n_striped_2_g_i_or_b_i_next_k0), .B_K1(n_striped_2_p_i_or_b_i_next_k1),
    .A_K0(n_striped_2_h_i_or_a_i_k0), .A_K1(n_striped_2_a_i_k1), .K_i(K5),
    .B_i_next(controlled_buffer_2_b_i_next), .A_i(controlled_buffer_2_a_i));
  n_X n_x_2 (
    .B_i_prev(controlled_buffer_3_b_i_next), .A_i(controlled_buffer_2_a_i), .g_i_prim(n_x_2_g_i_prim),
    .p_i_prim(n_x_2_p_i_prim), .h_i_prim(n_x_2_h_i_prim));
  Delay prim5 (
    .g_i(black_dot_3_g_i_i_prev), .p_i(black_dot_3_p_i_i_prev), .g_i_delay(prim5_g_i_delay),
    .p_i_delay(prim5_p_i_delay));
  Calc_Carry calc_carry_4 (
    .G_prev(C4_p_g_i_i_prev), .P_prev(C4_p_p_i_i_prev), .C_prev(calc_carry_6_c_i), .C_i(calc_carry_4_c_i));
  black_dot black_dot_3 (
    .p_i(n_x_2_p_i_prim), .p_i_prev(n_x_3_p_i_prim), .g_i(n_x_2_g_i_prim), .g_i_prev(n_x_3_g_i_prim),
    .g_i_i_prev(black_dot_3_g_i_i_prev), .p_i_i_prev(black_dot_3_p_i_i_prev));
  black_dot C5_p (
    .p_i(prim5_p_i_delay), .p_i_prev(prim3_p_i_i_prev), .g_i(prim5_g_i_delay), .g_i_prev(prim3_g_i_i_prev),
    .g_i_i_prev(C5_p_g_i_i_prev), .p_i_i_prev(C5_p_p_i_i_prev));
  Calc_Carry calc_carry_5 (
    .G_prev(C4_g_i_i_prev), .P_prev(C4_p_i_i_prev), .C_prev(calc_carry_7_c_i), .C_i(calc_carry_5_c_i));
  Tristate_Based_MUX tristate_based_mux_2 (
    .C_out(calc_carry_1_c_i), .H_i(h_delay_3_h_5_d), .H_i_prim(Prim_h_5_d), .C_i_prev(calc_carry_5_c_i),
    .C_i_prim_prev(calc_carry_4_c_i), .S_i(S5));
  black_dot black_dot_4 (
    .p_i(n_striped_2_p_i_or_b_i_next_k1), .p_i_prev(n_striped_3_p_i_or_b_i_next_k1),
    .g_i(n_striped_2_g_i_or_b_i_next_k0), .g_i_prev(n_striped_3_g_i_or_b_i_next_k0),
    .g_i_i_prev(black_dot_4_g_i_i_prev), .p_i_i_prev(black_dot_4_p_i_i_prev));
  Delay normal5 (
    .g_i(black_dot_4_g_i_i_prev), .p_i(black_dot_4_p_i_i_prev), .g_i_delay(normal5_g_i_delay),
    .p_i_delay(normal5_p_i_delay));
  black_dot C5 (
    .p_i(normal5_p_i_delay), .p_i_prev(normal3_p_i_i_prev), .g_i(normal5_g_i_delay),
    .g_i_prev(normal3_g_i_i_prev), .g_i_i_prev(C5_g_i_i_prev), .p_i_i_prev(C5_p_i_i_prev));
  n_striped n_striped_3 (
    .a_i(A4), .b_i(B4), .g_i_or_b_i_next_k0(n_striped_3_g_i_or_b_i_next_k0),
    .p_i_or_b_i_next_k1(n_striped_3_p_i_or_b_i_next_k1), .h_i_or_a_i_k0(n_striped_3_h_i_or_a_i_k0),
    .a_i_k1(n_striped_3_a_i_k1));
  Controlled_Buffer controlled_buffer_3 (
    .B_K0(n_striped_3_g_i_or_b_i_next_k0), .B_K1(n_striped_3_p_i_or_b_i_next_k1),
    .A_K0(n_striped_3_h_i_or_a_i_k0), .A_K1(n_striped_3_a_i_k1), .K_i(K4),
    .B_i_next(controlled_buffer_3_b_i_next), .A_i(controlled_buffer_3_a_i));
  n_X n_x_3 (
    .B_i_prev(controlled_buffer_4_b_i_next), .A_i(controlled_buffer_3_a_i), .g_i_prim(n_x_3_g_i_prim),
    .p_i_prim(n_x_3_p_i_prim), .h_i_prim(n_x_3_h_i_prim));
  Delay delay_3 (
    .g_i(n_x_3_g_i_prim), .p_i(n_x_3_p_i_prim), .g_i_delay(delay_3_g_i_delay), .p_i_delay(delay_3_p_i_delay));
  Delay prim4 (
    .g_i(delay_3_g_i_delay), .p_i(delay_3_p_i_delay), .g_i_delay(prim4_g_i_delay), .p_i_delay(prim4_p_i_delay));
  Calc_Carry calc_carry_6 (
    .G_prev(C3_p_g_i_delay), .P_prev(C3_p_p_i_delay), .C_prev(calc_carry_8_c_i), .C_i(calc_carry_6_c_i));
  Delay delay_4 (
    .g_i(n_striped_3_g_i_or_b_i_next_k0), .p_i(n_striped_3_p_i_or_b_i_next_k1),
    .g_i_delay(delay_4_g_i_delay), .p_i_delay(delay_4_p_i_delay));
  Delay normal4 (
    .g_i(delay_4_g_i_delay), .p_i(delay_4_p_i_delay), .g_i_delay(normal4_g_i_delay),
    .p_i_delay(normal4_p_i_delay));
  black_dot C4_p (
    .p_i(prim4_p_i_delay), .p_i_prev(prim3_p_i_i_prev), .g_i(prim4_g_i_delay), .g_i_prev(prim3_g_i_i_prev),
    .g_i_i_prev(C4_p_g_i_i_prev), .p_i_i_prev(C4_p_p_i_i_prev));
  Calc_Carry calc_carry_7 (
    .G_prev(C3_g_i_delay), .P_prev(C3_p_i_delay), .C_prev(calc_carry_9_c_i), .C_i(calc_carry_7_c_i));
  Tristate_Based_MUX tristate_based_mux_3 (
    .C_out(calc_carry_1_c_i), .H_i(h_delay_3_h_4_d), .H_i_prim(Prim_h_4_d), .C_i_prev(calc_carry_7_c_i),
    .C_i_prim_prev(calc_carry_6_c_i), .S_i(S4));
  black_dot C4 (
    .p_i(normal4_p_i_delay), .p_i_prev(normal3_p_i_i_prev), .g_i(normal4_g_i_delay),
    .g_i_prev(normal3_g_i_i_prev), .g_i_i_prev(C4_g_i_i_prev), .p_i_i_prev(C4_p_i_i_prev));
  n_striped n_striped_4 (
    .a_i(A3), .b_i(B3), .g_i_or_b_i_next_k0(n_striped_4_g_i_or_b_i_next_k0),
    .p_i_or_b_i_next_k1(n_striped_4_p_i_or_b_i_next_k1), .h_i_or_a_i_k0(n_striped_4_h_i_or_a_i_k0),
    .a_i_k1(n_striped_4_a_i_k1));
  Controlled_Buffer controlled_buffer_4 (
    .B_K0(n_striped_4_g_i_or_b_i_next_k0), .B_K1(n_striped_4_p_i_or_b_i_next_k1),
    .A_K0(n_striped_4_h_i_or_a_i_k0), .A_K1(n_striped_4_a_i_k1), .K_i(K3),
    .B_i_next(controlled_buffer_4_b_i_next), .A_i(controlled_buffer_4_a_i));
  n_X n_x_4 (
    .B_i_prev(controlled_buffer_5_b_i_next), .A_i(controlled_buffer_4_a_i), .g_i_prim(n_x_4_g_i_prim),
    .p_i_prim(n_x_4_p_i_prim), .h_i_prim(n_x_4_h_i_prim));
  black_dot black_dot_5 (
    .p_i(n_x_4_p_i_prim), .p_i_prev(n_x_5_p_i_prim), .g_i(n_x_4_g_i_prim), .g_i_prev(n_x_5_g_i_prim),
    .g_i_i_prev(black_dot_5_g_i_i_prev), .p_i_i_prev(black_dot_5_p_i_i_prev));
  black_dot prim3 (
    .p_i(black_dot_5_p_i_i_prev), .p_i_prev(black_dot_7_p_i_i_prev), .g_i(black_dot_5_g_i_i_prev),
    .g_i_prev(black_dot_7_g_i_i_prev), .g_i_i_prev(prim3_g_i_i_prev), .p_i_i_prev(prim3_p_i_i_prev));
  Delay C3_p (.g_i(prim3_g_i_i_prev), .p_i(prim3_p_i_i_prev), .g_i_delay(C3_p_g_i_delay), .p_i_delay(C3_p_p_i_delay));
  Calc_Carry calc_carry_8 (
    .G_prev(C2_p_g_i_delay), .P_prev(C2_p_p_i_delay), .C_prev(calc_carry_10_c_i), .C_i(calc_carry_8_c_i));
  Tristate_Based_MUX tristate_based_mux_4 (
    .C_out(calc_carry_1_c_i), .H_i(h_delay_3_h_3_d), .H_i_prim(Prim_h_3_d), .C_i_prev(calc_carry_9_c_i),
    .C_i_prim_prev(calc_carry_8_c_i), .S_i(S3));
  Delay C3 (.g_i(normal3_g_i_i_prev), .p_i(normal3_p_i_i_prev), .g_i_delay(C3_g_i_delay), .p_i_delay(C3_p_i_delay));
  Calc_Carry calc_carry_9 (
    .G_prev(C2_g_i_delay), .P_prev(C2_p_i_delay), .C_prev(calc_carry_11_c_i), .C_i(calc_carry_9_c_i));
  black_dot black_dot_6 (
    .p_i(n_striped_4_p_i_or_b_i_next_k1), .p_i_prev(n_striped_5_p_i_or_b_i_next_k1),
    .g_i(n_striped_4_g_i_or_b_i_next_k0), .g_i_prev(n_striped_5_g_i_or_b_i_next_k0),
    .g_i_i_prev(black_dot_6_g_i_i_prev), .p_i_i_prev(black_dot_6_p_i_i_prev));
  black_dot normal3 (
    .p_i(black_dot_6_p_i_i_prev), .p_i_prev(black_dot_8_p_i_i_prev), .g_i(black_dot_6_g_i_i_prev),
    .g_i_prev(black_dot_8_g_i_i_prev), .g_i_i_prev(normal3_g_i_i_prev), .p_i_i_prev(normal3_p_i_i_prev));
  n_striped n_striped_5 (
    .a_i(A2), .b_i(B2), .g_i_or_b_i_next_k0(n_striped_5_g_i_or_b_i_next_k0),
    .p_i_or_b_i_next_k1(n_striped_5_p_i_or_b_i_next_k1), .h_i_or_a_i_k0(n_striped_5_h_i_or_a_i_k0),
    .a_i_k1(n_striped_5_a_i_k1));
  Controlled_Buffer controlled_buffer_5 (
    .B_K0(n_striped_5_g_i_or_b_i_next_k0), .B_K1(n_striped_5_p_i_or_b_i_next_k1),
    .A_K0(n_striped_5_h_i_or_a_i_k0), .A_K1(n_striped_5_a_i_k1), .K_i(K2),
    .B_i_next(controlled_buffer_5_b_i_next), .A_i(controlled_buffer_5_a_i));
  n_X n_x_5 (
    .B_i_prev(controlled_buffer_6_b_i_next), .A_i(controlled_buffer_5_a_i), .g_i_prim(n_x_5_g_i_prim),
    .p_i_prim(n_x_5_p_i_prim), .h_i_prim(n_x_5_h_i_prim));
  Delay delay_5 (
    .g_i(n_x_5_g_i_prim), .p_i(n_x_5_p_i_prim), .g_i_delay(delay_5_g_i_delay), .p_i_delay(delay_5_p_i_delay));
  black_dot prim2 (
    .p_i(delay_5_p_i_delay), .p_i_prev(black_dot_7_p_i_i_prev), .g_i(delay_5_g_i_delay),
    .g_i_prev(black_dot_7_g_i_i_prev), .g_i_i_prev(prim2_g_i_i_prev), .p_i_i_prev(prim2_p_i_i_prev));
  Delay C2_p (.g_i(prim2_g_i_i_prev), .p_i(prim2_p_i_i_prev), .g_i_delay(C2_p_g_i_delay), .p_i_delay(C2_p_p_i_delay));
  Calc_Carry calc_carry_10 (
    .G_prev(C1_p_g_i_delay), .P_prev(C1_p_p_i_delay), .C_prev(C0_p_g_i_delay), .C_i(calc_carry_10_c_i));
  Tristate_Based_MUX tristate_based_mux_5 (
    .C_out(calc_carry_1_c_i), .H_i(h_delay_3_h_2_d), .H_i_prim(Prim_h_2_d), .C_i_prev(calc_carry_11_c_i),
    .C_i_prim_prev(calc_carry_10_c_i), .S_i(S2));
  Delay delay_6 (
    .g_i(n_striped_5_g_i_or_b_i_next_k0), .p_i(n_striped_5_p_i_or_b_i_next_k1),
    .g_i_delay(delay_6_g_i_delay), .p_i_delay(delay_6_p_i_delay));
  Delay C2 (.g_i(normal2_g_i_i_prev), .p_i(normal2_p_i_i_prev), .g_i_delay(C2_g_i_delay), .p_i_delay(C2_p_i_delay));
  Calc_Carry calc_carry_11 (
    .G_prev(C1_g_i_delay), .P_prev(C1_p_i_delay), .C_prev(C0_g_i_delay), .C_i(calc_carry_11_c_i));
  black_dot normal2 (
    .p_i(delay_6_p_i_delay), .p_i_prev(black_dot_8_p_i_i_prev), .g_i(delay_6_g_i_delay),
    .g_i_prev(black_dot_8_g_i_i_prev), .g_i_i_prev(normal2_g_i_i_prev), .p_i_i_prev(normal2_p_i_i_prev));
  n_striped n_striped_6 (
    .a_i(A1), .b_i(B1), .g_i_or_b_i_next_k0(n_striped_6_g_i_or_b_i_next_k0),
    .p_i_or_b_i_next_k1(n_striped_6_p_i_or_b_i_next_k1), .h_i_or_a_i_k0(n_striped_6_h_i_or_a_i_k0),
    .a_i_k1(n_striped_6_a_i_k1));
  Controlled_Buffer controlled_buffer_6 (
    .B_K0(n_striped_6_g_i_or_b_i_next_k0), .B_K1(n_striped_6_p_i_or_b_i_next_k1),
    .A_K0(n_striped_6_h_i_or_a_i_k0), .A_K1(n_striped_6_a_i_k1), .K_i(K1),
    .B_i_next(controlled_buffer_6_b_i_next), .A_i(controlled_buffer_6_a_i));
  n_X n_x_6 (
    .B_i_prev(controlled_buffer_7_b_i_next), .A_i(controlled_buffer_6_a_i), .g_i_prim(n_x_6_g_i_prim),
    .p_i_prim(n_x_6_p_i_prim), .h_i_prim(n_x_6_h_i_prim));
  black_dot black_dot_7 (
    .p_i(n_x_6_p_i_prim), .p_i_prev(n_x_7_p_i_prim), .g_i(n_x_6_g_i_prim), .g_i_prev(n_x_7_g_i_prim),
    .g_i_i_prev(black_dot_7_g_i_i_prev), .p_i_i_prev(black_dot_7_p_i_i_prev));
  Delay prim1 (
    .g_i(black_dot_7_g_i_i_prev), .p_i(black_dot_7_p_i_i_prev), .g_i_delay(prim1_g_i_delay),
    .p_i_delay(prim1_p_i_delay));
  Delay C1_p (.g_i(prim1_g_i_delay), .p_i(prim1_p_i_delay), .g_i_delay(C1_p_g_i_delay), .p_i_delay(C1_p_p_i_delay));
  Tristate_Based_MUX tristate_based_mux_6 (
    .C_out(calc_carry_1_c_i), .H_i(h_delay_3_h_1_d), .H_i_prim(Prim_h_1_d), .C_i_prev(C0_g_i_delay),
    .C_i_prim_prev(C0_p_g_i_delay), .S_i(S1));
  black_dot black_dot_8 (
    .p_i(n_striped_6_p_i_or_b_i_next_k1), .p_i_prev(n_striped_7_p_i_or_b_i_next_k1),
    .g_i(n_striped_6_g_i_or_b_i_next_k0), .g_i_prev(n_striped_7_g_i_or_b_i_next_k0),
    .g_i_i_prev(black_dot_8_g_i_i_prev), .p_i_i_prev(black_dot_8_p_i_i_prev));
  Delay normal1 (
    .g_i(black_dot_8_g_i_i_prev), .p_i(black_dot_8_p_i_i_prev), .g_i_delay(normal1_g_i_delay),
    .p_i_delay(normal1_p_i_delay));
  Delay C1 (.g_i(normal1_g_i_delay), .p_i(normal1_p_i_delay), .g_i_delay(C1_g_i_delay), .p_i_delay(C1_p_i_delay));
  not Cout (Cout_out, calc_carry_1_c_i);
  assign S0 = Cout_out ? h_delay_3_h_0_d : 1'bz;  // Controlled_Buffer_part H0
  n_striped n_striped_7 (
    .a_i(A0), .b_i(B0), .g_i_or_b_i_next_k0(n_striped_7_g_i_or_b_i_next_k0),
    .p_i_or_b_i_next_k1(n_striped_7_p_i_or_b_i_next_k1), .h_i_or_a_i_k0(n_striped_7_h_i_or_a_i_k0),
    .a_i_k1(n_striped_7_a_i_k1));
  Controlled_Buffer controlled_buffer_7 (
    .B_K0(n_striped_7_g_i_or_b_i_next_k0), .B_K1(n_striped_7_p_i_or_b_i_next_k1),
    .A_K0(n_striped_7_h_i_or_a_i_k0), .A_K1(n_striped_7_a_i_k1), .K_i(K0),
    .B_i_next(controlled_buffer_7_b_i_next), .A_i(controlled_buffer_7_a_i));
  n_X n_x_7 (
    .B_i_prev(1'b0), .A_i(controlled_buffer_7_a_i), .g_i_prim(n_x_7_g_i_prim), .p_i_prim(n_x_7_p_i_prim),
    .h_i_prim(n_x_7_h_i_prim));
  Delay delay_7 (
    .g_i(n_x_7_g_i_prim), .p_i(n_x_7_p_i_prim), .g_i_delay(delay_7_g_i_delay), .p_i_delay(delay_7_p_i_delay));
  Delay prim0 (
    .g_i(delay_7_g_i_delay), .p_i(delay_7_p_i_delay), .g_i_delay(prim0_g_i_delay), .p_i_delay(prim0_p_i_delay));
  Delay C0_p (.g_i(prim0_g_i_delay), .p_i(prim0_p_i_delay), .g_i_delay(C0_p_g_i_delay));  // open: p_i_delay
  assign S0 = calc_carry_1_c_i ? Prim_h_0_d : 1'bz;  // Controlled_Buffer_part H0_prim
  Delay delay_8 (
    .g_i(n_striped_7_g_i_or_b_i_next_k0), .p_i(n_striped_7_p_i_or_b_i_next_k1),
    .g_i_delay(delay_8_g_i_delay), .p_i_delay(delay_8_p_i_delay));
  Delay normal0 (
    .g_i(delay_8_g_i_delay), .p_i(delay_8_p_i_delay), .g_i_delay(normal0_g_i_delay),
    .p_i_delay(normal0_p_i_delay));
  Delay C0 (.g_i(normal0_g_i_delay), .p_i(normal0_p_i_delay), .g_i_delay(C0_g_i_delay));  // open: p_i_delay
endmodule

module Controlled_Buffer (
  input  B_K0,
  input  B_K1,
  input  A_K0,
  input  A_K1,
  input  K_i,
  output B_i_next,
  output A_i
);

  wire not_1_out, not_2_out;

  not not_1 (not_1_out, K_i);
  assign B_i_next = not_1_out ? B_K0 : 1'bz;  // Controlled_Buffer_part controlled_buffer_1
  assign B_i_next = K_i ? B_K1 : 1'bz;  // Controlled_Buffer_part controlled_buffer_2
  not not_2 (not_2_out, K_i);
  assign A_i = not_2_out ? A_K0 : 1'bz;  // Controlled_Buffer_part controlled_buffer_3
  assign A_i = K_i ? A_K1 : 1'bz;  // Controlled_Buffer_part controlled_buffer_4
endmodule

module Tristate_Based_MUX (
  input  C_out,
  input  H_i,
  input  H_i_prim,
  input  C_i_prev,
  input  C_i_prim_prev,
  output S_i
);

  wire controlled_buffer_1_out, controlled_buffer_3_out, not_1_out, not_2_out;

  not not_1 (not_1_out, C_out);
  assign controlled_buffer_1_out = not_1_out ? H_i : 1'bz;  // Controlled_Buffer_part controlled_buffer_1
  assign controlled_buffer_1_out = C_out ? H_i_prim : 1'bz;  // Controlled_Buffer_part controlled_buffer_2
  xor xor_1 (S_i, controlled_buffer_1_out, controlled_buffer_3_out);
  not not_2 (not_2_out, C_out);
  assign controlled_buffer_3_out = not_2_out ? C_i_prev : 1'bz;  // Controlled_Buffer_part controlled_buffer_3
  assign controlled_buffer_3_out = C_out ? C_i_prim_prev : 1'bz;  // Controlled_Buffer_part controlled_buffer_4
endmodule

module H_delay (
  input  H_6,
  input  H_5,
  input  H_4,
  input  H_3,
  input  H_2,
  input  H_1,
  input  H_0,
  output H_6_d,
  output H_5_d,
  output H_4_d,
  output H_3_d,
  output H_2_d,
  output H_1_d,
  output H_0_d
);

  buf buffer_1 (H_6_d, H_6);
  buf buffer_2 (H_5_d, H_5);
  buf buffer_3 (H_4_d, H_4);
  buf buffer_4 (H_3_d, H_3);
  buf buffer_5 (H_2_d, H_2);
  buf buffer_6 (H_1_d, H_1);
  buf buffer_7 (H_0_d, H_0);
endmodule

module Calc_Carry (
  input  G_prev,
  input  P_prev,
  input  C_prev,
  output C_i
);

  wire and_1_out;

  or or_1 (C_i, G_prev, and_1_out);
  and and_1 (and_1_out, P_prev, C_prev);
endmodule
